// Logisim project gate_progress.circ as structural Verilog: 1 circuit, main circuit main
module main (
  input  in_1
);

  // NOT_Gate not_1 is placed but not wired
  // Buffer buffer_1 is placed but not wired
  // AND_Gate and_1 is placed but not wired
  // OR_Gate or_1 is placed but not wired
  // NAND_Gate nand_1 is placed but not wired
  // NOR_Gate nor_1 is placed but not wired
  // XOR_Gate xor_1 is placed but not wired
  // NOT_Gate not_2 is placed but not wired
  // AND_Gate #(.width(1)) and_2: pin names not known; wires that end beside it: 1'b1, 4'b1100
  // OR_Gate or_2 is placed but not wired
  // NAND_Gate nand_2 is placed but not wired
  // NOR_Gate nor_2 is placed but not wired
  // XOR_Gate xor_2 is placed but not wired
  // XNOR_Gate xnor_1 is placed but not wired
  // AND_Gate and_3 is placed but not wired
  // OR_Gate or_3 is placed but not wired
  // NAND_Gate nand_3 is placed but not wired
  // NOR_Gate nor_3 is placed but not wired
  // XOR_Gate xor_3 is placed but not wired
  // XNOR_Gate xnor_2 is placed but not wired
  Multiplexer #(.select(1), .width(1)) multiplexer_1 ();  // open: in0, in1, out, sel
  Multiplexer #(.select(2), .width(1)) multiplexer_2 ();  // open: in0, in1, in2, in3, out, sel
  Multiplexer #(.select(3), .width(1)) multiplexer_3 ();  // open: in0, in1, in2, in3, in4, in5, in6, in7, out, sel
  Multiplexer #(.select(4), .width(1)) multiplexer_4 ();  // open: in0, in1, in2, in3, in4, in5, in6, in7, in8, in9, in10, in11, in12, in13, in14, in15, out, sel
  // XNOR_Gate xnor_3 is placed but not wired
  Adder #(.width(8)) adder_1 ();  // open: a, b, out, cin, cout
  Adder #(.width(8)) adder_2 ();  // open: a, b, out, cin, cout
  Adder #(.width(8)) adder_3 ();  // open: a, b, out, cin, cout
  D_Flip_Flop #(.trigger("rising")) d_ff_1 ();  // open: clk, D, Q, Qn, preset, en, reset
  LED led_1 ();  // open: in
  Button button_1 ();  // open: out
  Hex_Digit_Display hex_digit_display_1 ();  // open: value, dp
endmodule
